// Digital circuit and2_cmos.dig as structural Verilog
module and2_cmos (
  input  A,
  input  B,
  output Y
);

  wire N1_s, P1_d;

  PFET P1 (.G(A), .S(1'b1), .D(P1_d));
  NFET N1 (.G(A), .D(P1_d), .S(N1_s));
  NFET N2 (.G(B), .D(N1_s), .S(1'b0));
  PFET P2 (.G(B), .S(1'b1), .D(P1_d));
  PFET P3 (.G(P1_d), .S(1'b1), .D(Y));
  NFET N3 (.G(P1_d), .D(Y), .S(1'b0));

  // Notes on the sheet:
  //   CMOS AND (6T) = NAND (4T) + inverter (2T)
endmodule

/* Test case:
A B Y
0 0 0
0 1 0
1 0 0
1 1 1
*/
