// Digital circuit and2_nmos.dig as structural Verilog
module and2_nmos (
  input  A,
  input  B,
  output Y
);

  wire N1_s, pullup_1_out;

  PullUp pullup_1 (.out(pullup_1_out));
  NFET N1 (.G(A), .D(pullup_1_out), .S(N1_s));
  NFET N2 (.G(B), .D(N1_s), .S(1'b0));
  PullUp pullup_2 (.out(Y));
  NFET N3 (.G(pullup_1_out), .D(Y), .S(1'b0));
endmodule

/* Test case:
A B Y
0 0 0
0 1 0
1 0 0
1 1 1
*/
