// Digital circuit and2_pmos.dig as structural Verilog
module and2_pmos (
  input  A,
  input  B,
  output Y
);

  wire PA_d;

  PFET PA (.G(A), .S(1'b1), .D(PA_d));
  PullDown pulldown_1 (.out(PA_d));
  PFET PB (.G(B), .S(1'b1), .D(PA_d));
  PFET P3 (.G(PA_d), .S(1'b1), .D(Y));
  PullDown pulldown_2 (.out(Y));
endmodule

/* Test case:
A B Y
0 0 0
0 1 0
1 0 0
1 1 1
*/
