// Digital circuit inverter_pmos.dig as structural Verilog
module inverter_pmos (
  input  A,
  output Y
);

  PFET P1 (.G(A), .S(1'b1), .D(Y));
  PullDown pulldown_1 (.out(Y));
endmodule

/* Test case:
A Y
0 1
1 0
*/
