// Digital circuit nor2_pmos.dig as structural Verilog
module nor2_pmos (
  input  A,
  input  B,
  output Y
);

  wire P1_d;

  PFET P1 (.G(A), .S(1'b1), .D(P1_d));
  PFET P2 (.G(B), .S(P1_d), .D(Y));
  PullDown pulldown_1 (.out(Y));
endmodule

/* Test case:
A B Y
0 0 1
0 1 0
1 0 0
1 1 0
*/
