// Digital circuit or2_nmos.dig as structural Verilog
module or2_nmos (
  input  A,
  input  B,
  output Y
);

  wire pullup_1_out;

  PullUp pullup_1 (.out(pullup_1_out));
  NFET NA (.G(A), .D(pullup_1_out), .S(1'b0));
  NFET NB (.G(B), .D(pullup_1_out), .S(1'b0));
  PullUp pullup_2 (.out(Y));
  NFET N3 (.G(pullup_1_out), .D(Y), .S(1'b0));
endmodule

/* Test case:
A B Y
0 0 0
0 1 1
1 0 1
1 1 1
*/
