// Digital circuit or2_pmos.dig as structural Verilog
module or2_pmos (
  input  A,
  input  B,
  output Y
);

  wire P1_d, P2_d;

  PFET P1 (.G(A), .S(1'b1), .D(P1_d));
  PFET P2 (.G(B), .S(P1_d), .D(P2_d));
  PullDown pulldown_1 (.out(P2_d));
  PFET P3 (.G(P2_d), .S(1'b1), .D(Y));
  PullDown pulldown_2 (.out(Y));
endmodule

/* Test case:
A B Y
0 0 0
0 1 1
1 0 1
1 1 1
*/
