// Digital circuit xnor2_nmos.dig as structural Verilog
module xnor2_nmos (
  input  A,
  input  B,
  output Y
);

  wire NL1_s, NR1_s, pullup_1_out, pullup_2_out;

  PullUp pullup_1 (.out(pullup_1_out));
  NFET NiA (.G(A), .D(pullup_1_out), .S(1'b0));
  PullUp pullup_2 (.out(pullup_2_out));
  NFET NiB (.G(B), .D(pullup_2_out), .S(1'b0));
  PullUp pullup_3 (.out(Y));
  NFET NL1 (.G(A), .D(Y), .S(NL1_s));
  NFET NL2 (.G(pullup_2_out), .D(NL1_s), .S(1'b0));
  NFET NR1 (.G(pullup_1_out), .D(Y), .S(NR1_s));
  NFET NR2 (.G(B), .D(NR1_s), .S(1'b0));

  // Notes on the sheet:
  //   NMOS XNOR (6T + 3 pull-up loads)
endmodule

/* Test case:
A B Y
0 0 1
0 1 0
1 0 0
1 1 1
*/
