// Digital circuit xor2_pmos.dig as structural Verilog
module xor2_pmos (
  input  A,
  input  B,
  output Y
);

  wire PiA_d, PiB_d, PL1_d, PR1_d;

  PFET PiA (.G(A), .S(1'b1), .D(PiA_d));
  PullDown pulldown_1 (.out(PiA_d));
  PFET PiB (.G(B), .S(1'b1), .D(PiB_d));
  PullDown pulldown_2 (.out(PiB_d));
  PFET PL1 (.G(PiA_d), .S(1'b1), .D(PL1_d));
  PFET PL2 (.G(B), .S(PL1_d), .D(Y));
  PullDown pulldown_3 (.out(Y));
  PFET PR1 (.G(A), .S(1'b1), .D(PR1_d));
  PFET PR2 (.G(PiB_d), .S(PR1_d), .D(Y));

  // Notes on the sheet:
  //   PMOS XOR (6T + 3 pull-down loads)
endmodule

/* Test case:
A B Y
0 0 0
0 1 1
1 0 1
1 1 0
*/
